# Fritzing sketch Platine (saved by Fritzing 0.9.2b)
circuit board: 25cm x 25cm
circuit board: 10.5cm x 10.5cm
circuit board: 25cm x 1.2cm
circuit board: 7cm x 2.5cm
breadboards: 1

parts:
  Pi_- = Pad [width=4.5 height=4.5 connect=center]
  Pi_PWM = Pad [width=4.5 height=4.5 connect=center]
  Pi_+ = Pad [width=4.5 height=4.5 connect=center]
  Bat_+ = Pad [width=4.5 height=4.5 connect=center]
  Bat_- = Pad [width=4.5 height=4.5 connect=center]
  X6 = USB Connectors [package=usb-a-s]
  X4 = USB Connectors [package=usb-a-s]
  X3 = USB Connectors [package=usb-a-s]
  X7 = USB Connectors [package=usb-a-s]
  X8 = USB Connectors [package=usb-microb]
  Lade_- = Pad [width=4.2499346405228602 height=4.31633986928105 connect=center]
  Lade_+ = Pad [width=4.2499346405228602 height=4.31633986928105 connect=center]
  Pi_Switch1 = Pad [width=4.5 height=4.5 connect=center]
  S1 = SPST Switch [package=switch-spdt-smd]
  Pad3 = Pad [width=10 height=3 connect=center]
  Standart = USB Connectors [package=usb-a-pcb]
  Pad4 = Pad [width=16.2044327342185 height=3.2517490020964535 connect=center]  # not connected

nets:
  N1: Pi_-.pad, Bat_-.pad, S1.O
  N2: Pi_PWM.pad, X7.D-
  GND: Pi_+.pad, Bat_+.pad, X6.GND, X4.VBUS, X3.GND, X7.VBUS
  N3: X6.D+, X7.D+
  N4: X6.D-, X4.D-
  GND_2: X6.VBUS, X4.GND, X3.VBUS, X7.GND, S1.P
  N5: X4.D+, X3.D-
  N6: X3.D+, Pi_Switch1.pad
  N7: X8.GND, Lade_-.pad
  N8: X8.VBUS, Lade_+.pad
  N9: Pad3.pad, Standart.D+

notes:
  Usb gespiegelt
